# Fritzing sketch phone (saved by Fritzing 0.9.6b)
breadboards: 1

parts:
  R1 = Resistor [tolerance=±5% power=0.25W resistance=330k package=THT]
  D1 = Rectifier Diode [part_number=1N4001 package="300 mil [THT]"]
  D2 = Rectifier Diode [part_number=1N4001 package="300 mil [THT]"]
  D3 = Rectifier Diode [part_number=1N4001 package="300 mil [THT]"]
  R6 = Resistor [tolerance=±5% power=0.25W resistance=330k package=THT]
  R7 = Resistor [tolerance=±5% power=0.25W resistance=330k package=THT]
  R8 = Resistor [tolerance=±5% power=0.25W resistance=330k package=THT]
  R9 = Resistor [tolerance=±5% power=0.25W resistance=22k package=THT]
  S1 = Toggle Switch [package=THT]
  Part1 = Arduino Nano (Rev3.0)

nets:
  GND/GREEN: R1.Pin_0, R6.Pin_0, R7.Pin_0, R8.Pin_0, Part1.GND
  R1: R1.Pin_1, Part1.D10
  C1: D1.cathode
  N1: D1.anode, Part1.D3
  C2: D2.cathode
  N2: D2.anode, Part1.D5
  C3: D3.cathode
  N3: D3.anode, Part1.D4
  R3: R6.Pin_1, Part1.D8
  R2: R7.Pin_1, Part1.D9
  R4: R8.Pin_1, Part1.D7
  N4: R9.Pin_0, S1.L1
  RED: R9.Pin_1
  N5: S1.COM, Part1.D11/MOSI
  SPK: S1.L2

notes:
  PHONE BUTTONS
  HANDPIECE
